# Fritzing sketch bai2_debounce (saved by Fritzing 1.0.7)

parts:
  ESP32_DevKitC_V4 = ESP32_DevKitc_V4_1
  D1_-_Red_LED = LED - 5mm [color="Red (633nm)" current=0.030A package="5 mm [THT]"]
  SW1_-_Pushbutton = Pushbutton [package="[THT]"]
  R1_-_220_ohm = Resistor [tolerance=±5% power=0.25W resistance=220 package=THT]

nets:
  N1: ESP32_DevKitC_V4.connector23, R1_-_220_ohm.Pin_0
  N2: ESP32_DevKitC_V4.connector25, ESP32_DevKitC_V4.connector31, D1_-_Red_LED.cathode, SW1_-_Pushbutton.Pin_3, SW1_-_Pushbutton.Pin_4
  N3: D1_-_Red_LED.anode, R1_-_220_ohm.Pin_1
