# Fritzing sketch bai3a_adc1_filter_ledc (saved by Fritzing 1.0.7)

parts:
  ESP32_DevKitC_V4 = ESP32 DevKitc V4
  RV1_-_10k_Potentiometer = Rotary Potentiometer (Large) [Maximum_Resistance=10kΩ maximum_resistance=100kΩ knob_status=50% power=0.5W package=THT]
  R1_-_220_Ω = Resistor [Resistance=220 tolerance=±5% power=0.25W resistance=220 package=THT]
  D1_-_Red_LED = LED - 5mm [color="Red (633nm)" current=0.030A package="5 mm [THT]"]

nets:
  N1: ESP32_DevKitC_V4.Pin_1, RV1_-_10k_Potentiometer.leg1
  N2: ESP32_DevKitC_V4.Pin_5, RV1_-_10k_Potentiometer.wiper
  N3: ESP32_DevKitC_V4.Pin_14, ESP32_DevKitC_V4.Pin_32, RV1_-_10k_Potentiometer.leg2, D1_-_Red_LED.cathode
  N4: ESP32_DevKitC_V4.Pin_30, R1_-_220_Ω.Pin_0
  N5: R1_-_220_Ω.Pin_1, D1_-_Red_LED.anode

custom parts:
  ESP32 DevKitc V4: ESP32-DevKitC board with ESP32-WROOM-32 module. ESP32-DevKitC V4 is a small-sized ESP32-based development board produced by Espressif. Most of the pins on the ESP module are broken out to the pin headers on the board. The pins D0, D1, D2, D3, CMD and CLK are used internally for communication between ESP32 and SPI flash memory. They are grouped on both sides near the USB connector. Avoid using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
