# Fritzing sketch bai2_debounce (saved by Fritzing 1.0.8)
breadboards: 1

parts:
  A1 = ESP32 DevKitc V4
  S1 = Pushbutton [package="[SMD]"]
  LED1 = smd LED [color="Red (633nm)" package="0603 [SMD]"]

nets:
  N1: A1.Pin_24, LED1.anode
  N2: A1.Pin_26, S1.Pin_3, S1.Pin_4
  N3: A1.Pin_32, A1.Pin_38, S1.Pin_1, S1.Pin_2, LED1.cathode

custom parts:
  ESP32 DevKitc V4: ESP32-DevKitC board with ESP32-WROOM-32 module. ESP32-DevKitC V4 is a small-sized ESP32-based development board produced by Espressif. Most of the pins on the ESP module are broken out to the pin headers on the board. The pins D0, D1, D2, D3, CMD and CLK are used internally for communication between ESP32 and SPI flash memory. They are grouped on both sides near the USB connector. Avoid using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
