# Fritzing sketch bai3a_adc1_filter_ledc (saved by Fritzing 1.0.8)
breadboards: 1

parts:
  U1 = POT [knob_status=50% power=0.5W package=pot_mammoth]
  LED1 = smd LED [color="Red (633nm)" package="0603 [SMD]"]
  A1 = ESP32 DevKitc V4

nets:
  N1: U1.S, A1.Pin_14, A1.Pin_38
  N2: U1.A, A1.Pin_23
  N3: LED1.cathode, A1.Pin_1
  N4: LED1.anode, A1.Pin_30

custom parts:
  ESP32 DevKitc V4: ESP32-DevKitC board with ESP32-WROOM-32 module. ESP32-DevKitC V4 is a small-sized ESP32-based development board produced by Espressif. Most of the pins on the ESP module are broken out to the pin headers on the board. The pins D0, D1, D2, D3, CMD and CLK are used internally for communication between ESP32 and SPI flash memory. They are grouped on both sides near the USB connector. Avoid using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
