# Fritzing sketch vd1_dung_delay (saved by Fritzing 1.0.7)
circuit board: 8.46667cm x 5.64444cm
breadboards: 1

parts:
  A1 = ESP32 DevKitc V4
  LED1 = smd LED [color="Red (633nm)" package="1206 [SMD]"]
  R1 = Resistor [tolerance=±5% resistance=220 package="0603 [SMD]"]
  U1 = POT [knob_status=50% power=0.5W package=pot_alpha_rv16af-20]

nets:
  N1: A1.Pin_1, U1.E
  N2: A1.Pin_5, U1.S
  N3: A1.Pin_14, A1.Pin_38, LED1.cathode, U1.A
  N4: A1.Pin_24, R1.Pin_0
  N5: LED1.anode, R1.Pin_1

custom parts:
  ESP32 DevKitc V4: ESP32-DevKitC board with ESP32-WROOM-32 module. ESP32-DevKitC V4 is a small-sized ESP32-based development board produced by Espressif. Most of the pins on the ESP module are broken out to the pin headers on the board. The pins D0, D1, D2, D3, CMD and CLK are used internally for communication between ESP32 and SPI flash memory. They are grouped on both sides near the USB connector. Avoid using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
