# Fritzing sketch bai4_http (saved by Fritzing 1.0.7)
breadboards: 1

parts:
  A1 = ESP32 DevKitc V4
  R2 = Resistor [tolerance=±5% resistance=220 package="0402 [SMD]"]
  LED1 = LED - 3mm [color="Red (633nm)" current=0.030A package="3 mm [THT]"]

nets:
  N1: A1.Pin_12, R2.Pin_1
  N2: A1.Pin_14, A1.Pin_38, LED1.cathode
  N3: R2.Pin_0, LED1.anode

custom parts:
  ESP32 DevKitc V4: ESP32-DevKitC board with ESP32-WROOM-32 module. ESP32-DevKitC V4 is a small-sized ESP32-based development board produced by Espressif. Most of the pins on the ESP module are broken out to the pin headers on the board. The pins D0, D1, D2, D3, CMD and CLK are used internally for communication between ESP32 and SPI flash memory. They are grouped on both sides near the USB connector. Avoid using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
