# Fritzing sketch TH4-Bai2-MQTT-Publisher (saved by Fritzing 1.0.7)

parts:
  A1 = ESP32 DevKitc V4
  RHT1 = Humidity and Temperature Sensor RHT03

nets:
  N1: A1.Pin_1, RHT1.Vcc
  N2: A1.Pin_14, A1.Pin_38, RHT1.GND_2
  N3: A1.Pin_26, RHT1.Data-signal

custom parts:
  ESP32 DevKitc V4: ESP32-DevKitC board with ESP32-WROOM-32 module. ESP32-DevKitC V4 is a small-sized ESP32-based development board produced by Espressif. Most of the pins on the ESP module are broken out to the pin headers on the board. The pins D0, D1, D2, D3, CMD and CLK are used internally for communication between ESP32 and SPI flash memory. They are grouped on both sides near the USB connector. Avoid using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
