# Fritzing sketch TH4-Bai3-NodeRED-Dashboard (saved by Fritzing 1.0.7)

parts:
  A1 = ESP32 DevKitc V4
  LED1 = LED - 5mm [color="Red (633nm)" current=0.030A package="5 mm [THT]"]
  RHT1 = Humidity and Temperature Sensor RHT03
  R1 = Resistor [tolerance=±5% power=0.25W resistance=220 package=THT]

nets:
  N1: A1.Pin_1, RHT1.Vcc
  N2: A1.Pin_12, R1.Pin_0
  N3: A1.Pin_14, A1.Pin_32, A1.Pin_38, LED1.cathode, RHT1.GND_2
  N4: A1.Pin_26, RHT1.Data-signal
  N5: LED1.anode, R1.Pin_1

custom parts:
  ESP32 DevKitc V4: ESP32-DevKitC board with ESP32-WROOM-32 module. ESP32-DevKitC V4 is a small-sized ESP32-based development board produced by Espressif. Most of the pins on the ESP module are broken out to the pin headers on the board. The pins D0, D1, D2, D3, CMD and CLK are used internally for communication between ESP32 and SPI flash memory. They are grouped on both sides near the USB connector. Avoid using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
